# Fritzing sketch microview-dice (saved by Fritzing 0.9.3b)
breadboards: 1

parts:
  MV1 = MicroView [part_number=MicroView]
  S1 = Tilt Switch [package=THT]
  R1 = Rotary Potentiometer (Small) [maximum_resistance=100kΩ package=THT]

nets:
  N1: MV1.connector5, R1.wiper
  N2: MV1.connector6, S1.Pin_1, R1.leg1
  N3: MV1.connector9, S1.Pin_2
  N4: MV1.connector14, R1.leg2
